# Fritzing sketch Medicine alarm (saved by Fritzing 0.9.0b)
breadboards: 1

parts:
  Part1 = Arduino Uno (Rev3)
  LCD1 = LCD screen  # not connected
  Part2 = Real Time Clock Module - DS1307 RTC Breakout Board
  LED1 = LED - 3mm [color="Red (633nm)" package="3 mm [THT]"]
  LED2 = LED - 3mm [color="Green (570nm)" package="3 mm [THT]"]
  R1 = Resistor [tolerance=±5% resistance=220 package="0603 [SMD]"]
  R2 = Resistor [tolerance=±5% resistance=220 package="0603 [SMD]"]
  S1 = Pushbutton [package="[THT]"]
  S2 = Pushbutton [package="[THT]"]
  S3 = Pushbutton [package="[THT]"]
  S4 = Pushbutton [package="[THT]"]

nets:
  N1: Part1.A4/SDA, Part2.SDA
  N2: Part1.A5/SCL, Part2.SCL
  N3: Part1.D8, S2.Pin_1, S2.Pin_2
  N4: Part1.D10_PWM/SS, S1.Pin_1, S1.Pin_2
  N5: Part1.D13/SCK, LED2.cathode
  N6: Part1.D2, S4.Pin_1, S4.Pin_2
  N7: Part1.D3_PWM, S3.Pin_1, S3.Pin_2
  N8: Part1.D7, LED1.cathode
  5V: Part1.5V, Part2.5V
  GND: Part1.GND, Part2.GND, R1.Pin_0, S1.Pin_3, S1.Pin_4, S2.Pin_3, S2.Pin_4, S3.Pin_3, S3.Pin_4, S4.Pin_3, S4.Pin_4
  N9: LED1.anode, R2.Pin_1
  N10: LED2.anode, R1.Pin_1

notes:
  Medicine took in normal mode/ Change time unit in time modification mode
  Medalarm by Seyoung Park
  youngxotaniemi.wordpress.com
  LCD on in normal mode/ Change time when pressed long
  Increase in time change mode
  decrease in time change mode
  Remember to set buttons as INPUT_PULLUP
